# Fritzing sketch Sketch (saved by Fritzing 0.7.10b)
breadboards: 1

parts:
  Q1 = Basic FET P-Channel [package="TO220 [THT]"]
  R1 = Resistor [tolerance=±5% resistance=1 package=THT]
  Power_plug1 = Power plug
  S1 = Toggle Switch [package=THT]
  S2 = Toggle Switch [package=THT]
  VCC1 = Battery block 9V
  D1 = Rectifier Diode [part_number=1N4001 package="300 mil [THT]"]
  D2 = Rectifier Diode [part_number=1N4001 package="300 mil [THT]"]
  R2 = Resistor [tolerance=±5% resistance=10k package=THT]
  R3 = Resistor [tolerance=±5% resistance=10k package=THT]
  U1 = Voltage Regulator - 5V [package="TO220 [THT]"]
  C2 = Electrolytic Capacitor [capacitance=47µF package="100 mil [THT, electrolytic]"]
  J1 = female pin header, 1 pin [form="♀ (female)"]
  J2 = female pin header, 1 pin [form="♀ (female)"]
  LED1 = LED - 5mm [color="Infrared (940nm)" package="5 mm [THT]"]
  R4 = Resistor [tolerance=±5% resistance=100 package=THT]
  R5 = Photocell (LDR) [package=THT]
  R6 = Resistor [tolerance=±5% resistance=10k package=THT]
  LED2 = LED - 5mm [color="Red (633nm)" package="5 mm [THT]"]
  LED3 = LED - 5mm [color="Green (565nm)" package="5 mm [THT]"]
  LED4 = LED - 3mm [color="Red (633nm)" package="3 mm [THT]"]
  R8 = Resistor [tolerance=±5% resistance=220 package=THT]
  R9 = Resistor [tolerance=±5% resistance=1k package=THT]
  R10 = Resistor [tolerance=±5% resistance=100k package=THT]
  C3 = Ceramic Capacitor [capacitance=100nF package="100 mil [THT, multilayer]"]
  D4 = Rectifier Diode [part_number=1N4001 package="300 mil [THT]"]
  C1 = Electrolytic Capacitor [capacitance=0.1mF package="100 mil [THT, electrolytic]"]
  C4 = Ceramic Capacitor [capacitance=100nF package="100 mil [THT, multilayer]"]
  R11 = Resistor [tolerance=±5% resistance=100k package=THT]
  Arduino1 = Arduino
  R7 = Resistor [tolerance=±5% resistance=220 package=THT]
  R12 = Resistor [tolerance=±5% resistance=220 package=THT]
  S3 = Pushbutton [package="[THT]"]

nets:
  N1: Q1.gate, C4.1, R11.Pin_1
  N2: Q1.drain, J2.pin1, R10.Pin_1, C3.1, Arduino1.A1
  N3: Q1.source, R1.Pin_0, D4.cathode
  GND: R1.Pin_1, Power_plug1.GND, VCC1.-, R3.Pin_1, U1.GND, C2.-, J1.pin1, R4.Pin_0, R6.Pin_1, LED2.cathode, LED3.cathode, LED4.cathode, R10.Pin_0, C3.0, D4.anode, C1.-, R11.Pin_0, Arduino1.GND
  N4: Power_plug1.VCC, S1.L1
  N5: S1.COM, D1.anode
  N6: S2.L1, VCC1.+
  N7: S2.COM, D2.anode, R2.Pin_0
  N8: D1.cathode, D2.cathode, U1.input_voltage, C1.+
  N9: R2.Pin_1, R3.Pin_0, Arduino1.A0
  N10: U1.output_voltage, C2.+, LED1.cathode, R5.pin_0, Arduino1.+5V, S3.Pin_3, S3.Pin_4
  N11: LED1.anode, R4.Pin_1
  N12: R5.pin_1, R6.Pin_0, Arduino1.D3
  N13: LED2.anode, R8.Pin_0
  N14: LED3.anode, R7.Pin_0
  N15: LED4.anode, R9.Pin_0
  N16: R8.Pin_1, Arduino1.D9
  N17: R9.Pin_1, Arduino1.D10
  N18: C4.0, Arduino1.D13
  N19: Arduino1.D8, R7.Pin_1
  N20: R12.Pin_1, S3.Pin_2

notes:
  5V
  Gnd
  batt
  DC-in
  servo1
